# Fritzing sketch Schematic (saved by Fritzing 0.8.5b)

parts:
  S1 = SWITCH-MOMENTARY-2 [package=reed_switch_plastic]
  R2 = Resistor [tolerance=±5% resistance=10k package=THT]
  LED1 = LED - 5mm [color="Red (633nm)" package="5 mm [THT]"]
  LED2 = LED - 5mm [color="Red (633nm)" package="5 mm [THT]"]
  LED3 = LED - 5mm [color="Red (633nm)" package="5 mm [THT]"]
  LED4 = LED - 5mm [color="Red (633nm)" package="5 mm [THT]"]
  LED5 = LED - 5mm [color="Red (633nm)" package="5 mm [THT]"]
  LED6 = LED - 5mm [color="Red (633nm)" package="5 mm [THT]"]
  LED7 = LED - 5mm [color="Red (633nm)" package="5 mm [THT]"]
  LED8 = LED - 5mm [color="Red (633nm)" package="5 mm [THT]"]
  LED9 = LED - 5mm [color="Red (633nm)" package="5 mm [THT]"]
  LED10 = LED - 5mm [color="Red (633nm)" package="5 mm [THT]"]
  LED11 = LED - 5mm [color="Red (633nm)" package="5 mm [THT]"]
  LED12 = LED - 5mm [color="Red (633nm)" package="5 mm [THT]"]
  R1 = Resistor [tolerance=±5% resistance=33 package=THT]
  Part1 = Arduino Uno (Rev3) - ICSP

nets:
  N1: S1.1, Part1.5V
  N2: S1.2, R2.Pin_0, Part1.D3_PWM
  N3: R2.Pin_1, R1.Pin_1, Part1.GND
  N4: LED1.cathode, Part1.D0/RX
  N5: LED1.anode, LED2.anode, LED3.anode, LED4.anode, LED5.anode, LED6.anode, LED7.anode, LED8.anode, LED9.anode, LED10.anode, LED11.anode, LED12.anode, R1.Pin_0
  N6: LED2.cathode, Part1.D1/TX
  N7: LED3.cathode, Part1.D2
  N8: LED4.cathode, Part1.D5_PWM
  N9: LED5.cathode, Part1.D6_PWM
  N10: LED6.cathode, Part1.D7
  N11: LED7.cathode, Part1.D8
  N12: LED8.cathode, Part1.D9_PWM
  N13: LED9.cathode, Part1.D10_PWM/SS
  N14: LED10.cathode, Part1.D11_PWM/MOSI
  N15: LED11.cathode, Part1.D12/MISO
  N16: LED12.cathode, Part1.D13/SCK
